// Logisim project counter.circ as structural Verilog: 2 circuits, main circuit main
module main (
);

  wire button_1_out, clock_1_out, d_ff_1_q, d_ff_2_q, d_ff_3_q, d_ff_4_q, n4bit_1_at, n4bit_1_bt, n4bit_1_ct,
       n4bit_1_dt, n7segment_1_a_2, n7segment_1_b_2, n7segment_1_c_2, n7segment_1_d_2, n7segment_1_e,
       n7segment_1_f, n7segment_1_g, or_1_out;

  Clock clock_1 (.out(clock_1_out));
  Button button_1 (.out(button_1_out));
  or or_1 (or_1_out, clock_1_out, button_1_out);
  D_Flip_Flop d_ff_1 (.clk(or_1_out), .D(n4bit_1_at), .Q(d_ff_1_q));  // open: Qn, preset, en, reset
  D_Flip_Flop d_ff_2 (.clk(or_1_out), .D(n4bit_1_bt), .Q(d_ff_2_q));  // open: Qn, preset, en, reset
  D_Flip_Flop d_ff_3 (.clk(or_1_out), .D(n4bit_1_ct), .Q(d_ff_3_q));  // open: Qn, preset, en, reset
  D_Flip_Flop d_ff_4 (.clk(or_1_out), .D(n4bit_1_dt), .Q(d_ff_4_q));  // open: Qn, preset, en, reset
  _4bit u_4bit_1 (
    .A(d_ff_1_q), .B(d_ff_2_q), .C(d_ff_3_q), .D(d_ff_4_q), .AT(n4bit_1_at), .BT(n4bit_1_bt),
    .CT(n4bit_1_ct), .DT(n4bit_1_dt));
  _7segment u_7segment_1 (
    .A(n4bit_1_at), .B(n4bit_1_bt), .C(n4bit_1_ct), .D(n4bit_1_dt), .a_2(n7segment_1_a_2),
    .b_2(n7segment_1_b_2), .c_2(n7segment_1_c_2), .d_2(n7segment_1_d_2), .e(n7segment_1_e),
    .f(n7segment_1_f), .g(n7segment_1_g));
  _7_Segment_Display u_7_segment_display_1 (
    .g(n7segment_1_g), .f(n7segment_1_f), .a(n7segment_1_a_2), .b(n7segment_1_b_2), .e(n7segment_1_e),
    .d(n7segment_1_d_2), .c(n7segment_1_c_2));  // open: dp
endmodule

module _4bit (
  input  A,
  input  B,
  input  C,
  input  D,
  output AT,
  output BT,
  output CT,
  output DT
);

  wire and_1_out, and_2_out, and_3_out, and_4_out, and_5_out, and_6_out, and_7_out, and_8_out, and_9_out,
       not_1_out, not_2_out, not_3_out, not_4_out, not_5_out, not_6_out, not_7_out, not_8_out, not_9_out;

  not not_1 (not_1_out, A);
  not not_2 (not_2_out, B);
  not not_3 (not_3_out, C);
  not not_4 (not_4_out, D);
  not not_5 (not_5_out, B);
  and and_1 (and_1_out, not_5_out, C, D);
  and and_2 (and_2_out, B, not_6_out);
  not not_6 (not_6_out, C);
  and and_3 (and_3_out, B, not_7_out);
  not not_7 (not_7_out, D);
  not not_8 (not_8_out, C);
  and and_4 (and_4_out, not_8_out, D);
  and and_5 (and_5_out, C, not_9_out);
  not not_9 (not_9_out, D);
  not not_10 (DT, D);
  and and_6 (and_6_out, not_1_out, B, C, D);
  and and_7 (and_7_out, A, not_2_out);
  and and_8 (and_8_out, A, not_3_out);
  and and_9 (and_9_out, A, not_4_out);
  or or_1 (BT, and_1_out, and_2_out, and_3_out);
  or or_2 (CT, and_4_out, and_5_out);
  or or_3 (AT, and_6_out, and_7_out, and_8_out, and_9_out);
endmodule
